// Logisim project P2_Logica_Digital.circ as structural Verilog
module inversor3bits (
  input  e2,
  input  e1,
  input  e0,
  input  in_4,
  output s2,
  output s1,
  output s0
);

  xor xor_1 (s2, in_4, e2);
  xor xor_2 (s1, in_4, e1);
  xor xor_3 (s0, in_4, e0);
endmodule

module inversoAdCompA2 (
  input  e3,
  input  e2,
  input  e1,
  input  e0,
  output err,
  output s3,
  output s2,
  output s1,
  output s0
);

  wire and_1_out, and_2_out, and_3_out, and_4_out, and_5_out, and_6_out, and_7_out, and_8_out, not_1_out,
       not_2_out, not_3_out, not_4_out, not_5_out, not_6_out, not_7_out, not_8_out, xor_2_out, xor_3_out,
       xor_5_out, xor_6_out, xor_8_out, xor_9_out, xor_11_out;

  xor xor_1 (err, and_1_out, and_2_out);
  and and_1 (and_1_out, not_2_out, not_1_out);
  and and_2 (and_2_out, xor_3_out, xor_2_out);
  not not_1 (not_1_out, e3);
  xor xor_2 (xor_2_out, not_1_out, not_2_out);
  not not_2 (not_2_out, 1'b1);
  xor xor_3 (xor_3_out, and_3_out, and_4_out);
  xor xor_4 (s3, xor_2_out, xor_3_out);
  and and_3 (and_3_out, not_4_out, not_3_out);
  and and_4 (and_4_out, xor_6_out, xor_5_out);
  not not_3 (not_3_out, e2);
  xor xor_5 (xor_5_out, not_3_out, not_4_out);
  not not_4 (not_4_out, 1'b1);
  xor xor_6 (xor_6_out, and_5_out, and_6_out);
  xor xor_7 (s2, xor_5_out, xor_6_out);
  and and_5 (and_5_out, not_6_out, not_5_out);
  and and_6 (and_6_out, xor_9_out, xor_8_out);
  not not_5 (not_5_out, e1);
  xor xor_8 (xor_8_out, not_5_out, not_6_out);
  not not_6 (not_6_out, 1'b1);
  xor xor_9 (xor_9_out, and_7_out, and_8_out);
  xor xor_10 (s1, xor_8_out, xor_9_out);
  and and_7 (and_7_out, 1'b1, not_7_out);
  and and_8 (and_8_out, not_8_out, xor_11_out);
  not not_7 (not_7_out, e0);
  xor xor_11 (xor_11_out, not_7_out, 1'b1);
  not not_8 (not_8_out, 1'b1);
  xor xor_12 (s0, xor_11_out, not_8_out);
endmodule

module demultiplexor (
  input  c1,
  input  c0,
  input  e0,
  output s3,
  output s2,
  output s1,
  output s0
);

  wire not_1_out, not_2_out, not_3_out, not_4_out;

  and and_1 (s3, e0, c1, c0);
  and and_2 (s2, e0, c1, not_1_out);
  not not_1 (not_1_out, c0);
  not not_2 (not_2_out, c1);
  and and_3 (s1, e0, not_2_out, c0);
  not not_3 (not_3_out, c1);
  and and_4 (s0, e0, not_3_out, not_4_out);
  not not_4 (not_4_out, c0);
endmodule
